# Fritzing sketch schematic (saved by Fritzing 0.9.3b)
breadboards: 1

parts:
  U1 = NodeMCU V3.0
  S1 = Pushbutton [package="[THT]"]
  S2 = Pushbutton [package="[THT]"]
  S3 = Toggle Switch [package=THT]
  LED1 = smd LED [color="Blue (470nm)" package="1206 [SMD]"]
  R1 = Resistor [tolerance=±5% resistance=220 package=THT]
  R2 = Resistor [tolerance=±5% resistance=2.2k package=THT]
  KY-1 = Keyes Relay [package=THT]

nets:
  N1: U1.D2, S2.Pin_3, S2.Pin_4
  N2: U1.3V3, R2.Pin_0, KY-1.power
  N3: U1.GND, S1.Pin_3, S1.Pin_4, S2.Pin_1, S2.Pin_2, S3.L2, R1.Pin_0, KY-1.ground
  N4: U1.D5, KY-1.signal
  N5: U1.D6, LED1.anode
  N6: U1.D7, S3.COM, R2.Pin_1
  N7: U1.RX, S1.Pin_1, S1.Pin_2
  N8: LED1.cathode, R1.Pin_1

custom parts:
  NodeMCU V3.0: ESP8266 based NodeMCU
  Keyes Relay: The Keyes 5V relay module is suitable for SCM development, home appliance control. It uses a 5V~12V TIL control signal which can control DC / AC signal.
